# Fritzing sketch Thermometer-Attiny85 (saved by Fritzing 0.9.3b)
circuit board: 8.46667cm x 5.64444cm
breadboards: 1

parts:
  U1 = attiny85 [package=dip]
  Q1 = TRANSISTOR_NPN [part_number=A42 package=to-92]
  R1 = Resistor [tolerance=±20% resistance=1M package="1206 [SMD]"]
  R2 = Resistor [tolerance=±20% resistance=220 package="1206 [SMD]"]
  LED1 = smd LED [color="Red (633nm)" package="0805 [SMD]"]

nets:
  GND: U1.Pin_4, Q1.E
  N1: U1.Pin_6, R1.Pin_0
  3.3V: U1.Pin_8, LED1.anode
  N2: Q1.B, R1.Pin_1
  N3: Q1.C, R2.Pin_1
  N4: R2.Pin_0, LED1.cathode
